# Fritzing sketch MonitorStand (saved by Fritzing 0.9.3b)
breadboards: 1

parts:
  Part1 = Triple Axis Accelerometer Breakout - ADXL335
  WeMos_D1_Mini1 = WeMos D1 Mini
  hc-sr1 = hc-sr04
  R1 = Resistor [tolerance=±5% resistance=220 package=THT]
  R2 = Resistor [tolerance=±5% resistance=220 package=THT]
  R3 = Resistor [tolerance=±5% resistance=220 package=THT]
  R4 = Resistor [tolerance=±5% resistance=220 package=THT]

nets:
  N1: Part1.ZOUT, R3.Pin_1
  N2: Part1.YOUT, R2.Pin_1
  N3: Part1.XOUT, R1.Pin_1
  GND: Part1.GND, WeMos_D1_Mini1.G, hc-sr1.GND
  VCC: Part1.VCC, WeMos_D1_Mini1.5V, hc-sr1.VCC
  N4: WeMos_D1_Mini1.A0, R4.Pin_0
  N5: WeMos_D1_Mini1.D3, hc-sr1.Trig
  N6: WeMos_D1_Mini1.D5, hc-sr1.Echo
  N7: R1.Pin_0, R2.Pin_0, R3.Pin_0
